// Logisim project WITCPU.circ as structural Verilog: 5 circuits, main circuit register_group
module register_group (
  input  [15:0] Data,
  input  Clock,
  input  [1:0] Ra,
  input  [1:0] Rd,
  input  [1:0] Rb,
  output [15:0] x_Output,
  output [15:0] out_7
);

  wire demultiplexer_1_out0, demultiplexer_1_out1, demultiplexer_1_out2, demultiplexer_1_out3;
  wire [15:0] register_1_q, register_2_q, register_3_q, register_4_q;

  Demultiplexer #(.select(2)) demultiplexer_1 (
    .out0(demultiplexer_1_out0), .out1(demultiplexer_1_out1), .out2(demultiplexer_1_out2),
    .out3(demultiplexer_1_out3), .in(Clock), .sel(Rd));  // open: en
  Register #(.width(16)) register_1 (.D(Data), .Q(register_1_q), .clk(demultiplexer_1_out0));  // open: en, clr
  Register #(.width(16)) register_2 (.D(Data), .Q(register_2_q), .clk(demultiplexer_1_out1));  // open: en, clr
  Register #(.width(16)) register_3 (.D(Data), .Q(register_3_q), .clk(demultiplexer_1_out2));  // open: en, clr
  Register #(.width(16)) register_4 (.D(Data), .Q(register_4_q), .clk(demultiplexer_1_out3));  // open: en, clr
  Multiplexer #(.select(2), .width(16)) multiplexer_1 (
    .in0(register_1_q), .in1(register_2_q), .in2(register_3_q), .in3(register_4_q), .out(x_Output), .sel(Ra));  // open: en
  Multiplexer #(.select(2), .width(16)) multiplexer_2 (
    .in0(register_1_q), .in1(register_2_q), .in2(register_3_q), .in3(register_4_q), .out(out_7), .sel(Rb));  // open: en
endmodule

module registers (
  input  [15:0] Rd_value,
  input  Clock,
  input  [3:0] Rd,
  input  [1:0] Ry,
  input  [1:0] Rx,
  output [15:0] out_6,
  output [15:0] out_7
);

  wire demultiplexer_1_out0, demultiplexer_1_out1, demultiplexer_1_out2, demultiplexer_1_out3;
  wire [15:0] R0_R3_out_6, R0_R3_out_7, R4___R7_out_7, R4___R7_x_output, R8_Rb_out_7, R8_Rb_x_output,
       Rc_Rf_out_7, Rc_Rf_x_output;

  Demultiplexer #(.select(2)) demultiplexer_1 (
    .out0(demultiplexer_1_out0), .out1(demultiplexer_1_out1), .out2(demultiplexer_1_out2),
    .out3(demultiplexer_1_out3), .in(Clock), .sel(Rd[1:0]));  // open: en
  register_group_r0 R0_R3 (
    .Data(Rd_value), .Clock(demultiplexer_1_out0), .Ra(Rx), .Rd(Rd[3:2]), .Rb(Ry), .out_6(R0_R3_out_6),
    .out_7(R0_R3_out_7));
  register_group R4___R7 (
    .Data(Rd_value), .Clock(demultiplexer_1_out1), .Ra(Rx), .Rd(Rd[3:2]), .Rb(Ry),
    .x_Output(R4___R7_x_output), .out_7(R4___R7_out_7));
  register_group R8_Rb (
    .Data(Rd_value), .Clock(demultiplexer_1_out2), .Ra(Rx), .Rd(Rd[3:2]), .Rb(Ry), .x_Output(R8_Rb_x_output),
    .out_7(R8_Rb_out_7));
  register_group Rc_Rf (
    .Data(Rd_value), .Clock(demultiplexer_1_out3), .Ra(Rx), .Rd(Rd[3:2]), .Rb(Ry), .x_Output(Rc_Rf_x_output),
    .out_7(Rc_Rf_out_7));
  Multiplexer #(.select(2), .width(16)) multiplexer_1 (
    .in0(R0_R3_out_6), .in1(R4___R7_x_output), .in2(R8_Rb_out_7), .in3(Rc_Rf_x_output), .out(out_6),
    .sel(Rd[1:0]));  // open: en
  Multiplexer #(.select(2), .width(16)) multiplexer_2 (
    .in0(R0_R3_out_7), .in1(R4___R7_out_7), .in2(R8_Rb_x_output), .in3(Rc_Rf_out_7), .out(out_7),
    .sel(Rd[1:0]));  // open: en
endmodule

module register_group_r0 (
  input  [15:0] Data,
  input  Clock,
  input  [1:0] Ra,
  input  [1:0] Rd,
  input  [1:0] Rb,
  output [15:0] out_6,
  output [15:0] out_7
);

  wire demultiplexer_1_out0, demultiplexer_1_out1, demultiplexer_1_out2, demultiplexer_1_out3;
  wire [15:0] register_1_q, register_2_q, register_3_q, register_4_q;

  Demultiplexer #(.select(2)) demultiplexer_1 (
    .out0(demultiplexer_1_out0), .out1(demultiplexer_1_out1), .out2(demultiplexer_1_out2),
    .out3(demultiplexer_1_out3), .in(Clock), .sel(Rd));  // open: en
  Register #(.width(16)) register_1 (.D({16{1'b0}}), .Q(register_1_q), .clk(demultiplexer_1_out0));  // open: en, clr
  Register #(.width(16)) register_2 (.D(Data), .Q(register_2_q), .clk(demultiplexer_1_out1));  // open: en, clr
  Register #(.width(16)) register_3 (.D(Data), .Q(register_3_q), .clk(demultiplexer_1_out2));  // open: en, clr
  Register #(.width(16)) register_4 (.D(Data), .Q(register_4_q), .clk(demultiplexer_1_out3));  // open: en, clr
  Multiplexer #(.select(2), .width(16)) multiplexer_1 (
    .in0(register_1_q), .in1(register_2_q), .in2(register_3_q), .in3(register_4_q), .out(out_6), .sel(Ra));  // open: en
  Multiplexer #(.select(2), .width(16)) multiplexer_2 (
    .in0(register_1_q), .in1(register_2_q), .in2(register_3_q), .in3(register_4_q), .out(out_7), .sel(Rb));  // open: en
endmodule

module alu (
  input  [15:0] Data1,
  input  [15:0] Data2,
  input  [3:0] OpCode,
  input  Enable,
  input  [7:0] Immediate,
  output [15:0] out_6
);

  wire [15:0] adder_1_out, and_1_out, bit_extender_1_out, divider_1_out, multiplier_1_out, or_1_out,
       subtractor_1_out, xnor_1_out;

  Adder #(.width(16)) adder_1 (.a(Data1), .b(Data2), .out(adder_1_out));  // open: cin, cout
  Subtractor #(.width(16)) subtractor_1 (.a(Data1), .b(Data2), .out(subtractor_1_out));  // open: bin, bout
  Multiplier #(.width(16)) multiplier_1 (.a(Data1), .b(Data2), .out(multiplier_1_out));  // open: cin, cout
  Divider #(.width(16)) divider_1 (.a(Data1), .b(Data2), .out(divider_1_out));  // open: upper, rem
  assign and_1_out = Data1 & Data2;  // AND_Gate and_1, 16 bits wide
  assign or_1_out = Data1 | Data2;  // OR_Gate or_1, 16 bits wide
  assign bit_extender_1_out = {{8{Immediate[7]}}, Immediate};  // Bit_Extender bit_extender_1
  assign xnor_1_out = ~(Data1 ^ Data2);  // XNOR_Gate xnor_1, 16 bits wide
  Multiplexer #(.select(3), .width(16)) multiplexer_1 (
    .in0(adder_1_out), .in1(subtractor_1_out), .in2(multiplier_1_out), .in3(divider_1_out), .in4(and_1_out),
    .in5(or_1_out), .in6(xnor_1_out), .in7(bit_extender_1_out), .out(out_6), .sel(OpCode[2:0]), .en(Enable));
endmodule

module decoder (
  input  [15:0] Instruction,
  output [3:0] OpCode,
  output [3:0] Operand1,
  output [3:0] Operand2,
  output [3:0] Operand3,
  output [7:0] Immediate
);

  Multiplexer #(.width(4)) multiplexer_1 (
    .in0(Instruction[7:4]), .in1(Instruction[3:0]), .out(Operand2), .sel(Instruction[15]));  // open: en
  Multiplexer #(.width(8)) multiplexer_2 (
    .in0({8{1'b0}}), .in1(Instruction[11:4]), .out(Immediate), .sel(Instruction[15]));  // open: en

  assign OpCode = Instruction[15:12];
  assign Operand1 = Instruction[3:0];
  assign Operand3 = Instruction[11:8];
endmodule
